// Logisim project full subractor using 2 half subtractor.circ as structural Verilog: 1 circuit, main circuit main
module main (
  input  in_1,
  input  in_2,
  input  in_3,
  output out_4,
  output out_5
);

  wire and_1_out, and_2_out, not_1_out, not_2_out, xor_1_out;

  xor xor_1 (xor_1_out, in_1, in_2);
  xor xor_2 (out_4, xor_1_out, in_3);
  not not_1 (not_1_out, xor_1_out);
  not not_2 (not_2_out, in_1);
  and and_1 (and_1_out, not_1_out, in_3);
  and and_2 (and_2_out, not_2_out, in_2);
  or or_1 (out_5, and_1_out, and_2_out);
endmodule
